// Digital circuit Lab02.dig as structural Verilog
module Lab02 (
  input  B,
  input  C,
  input  A,
  input  D,
  output Fa,
  output Fb,
  output Fc,
  output Fd,
  output Fe,
  output Fg,
  output Ff
);

  wire Ai, and_1_out, and_2_out, and_3_out, and_4_out, and_5_out, and_6_out, and_7_out, and_8_out, and_9_out,
       and_10_out, and_11_out, and_12_out, and_13_out, and_14_out, and_15_out, and_16_out, and_17_out,
       and_18_out, and_19_out, and_20_out, and_21_out, and_22_out, and_23_out, and_24_out, and_25_out,
       and_26_out, and_27_out, and_28_out, and_29_out, and_30_out, and_31_out, and_32_out, Bi, Ci, Di;

  and and_1 (and_1_out, Ai, B, Ci);
  and and_2 (and_2_out, A, Bi);
  and and_3 (and_3_out, A, C);
  and and_4 (and_4_out, B, C, Di);
  and and_5 (and_5_out, Bi, Ci, Di);
  or or_1 (Ff, and_1_out, and_2_out, and_3_out, and_4_out, and_5_out);
  not not_1 (Bi, B);
  not not_2 (Ci, C);
  not not_3 (Di, D);
  and and_6 (and_6_out, A, Bi, Ci);
  and and_7 (and_7_out, Ai, B, D);
  and and_8 (and_8_out, Bi, Di);
  and and_9 (and_9_out, Ai, C);
  and and_10 (and_10_out, B, C);
  not not_4 (Ai, A);
  or or_2 (Fa, and_6_out, and_7_out, and_8_out, and_9_out, and_10_out);
  and and_11 (and_11_out, Ai, Ci, Di);
  and and_12 (and_12_out, Ai, C, D);
  and and_13 (and_13_out, A, Ci, D);
  and and_14 (and_14_out, Bi, Di);
  and and_15 (and_15_out, Bi, Ci);
  or or_3 (Fb, and_11_out, and_12_out, and_13_out, and_14_out, and_15_out);
  Seven_Seg seven_seg_1 (.a(Fa), .b(Fb), .c(Fc), .d(Fd), .e(Fe), .f(Ff), .g(Fg), .dp(1'b0));
  and and_16 (and_16_out, Ci, D);
  and and_17 (and_17_out, Ai, B);
  and and_18 (and_18_out, A, Bi);
  and and_19 (and_19_out, Bi, D);
  and and_20 (and_20_out, Bi, Ci);
  or or_4 (Fc, and_16_out, and_17_out, and_18_out, and_19_out, and_20_out);
  and and_21 (and_21_out, Bi, C);
  and and_22 (and_22_out, B, Ci);
  and and_23 (and_23_out, B, Di);
  or or_5 (Fg, and_21_out, and_22_out, and_23_out, A);
  and and_24 (and_24_out, B, Ci, D);
  and and_25 (and_25_out, A, Ci);
  and and_26 (and_26_out, B, C, Di);
  and and_27 (and_27_out, Bi, C, D);
  and and_28 (and_28_out, Ai, Bi, Di);
  or or_6 (Fd, and_24_out, and_25_out, and_26_out, and_27_out, and_28_out);
  and and_29 (and_29_out, Bi, Di);
  and and_30 (and_30_out, C, Di);
  and and_31 (and_31_out, A, C);
  and and_32 (and_32_out, A, B);
  or or_7 (Fe, and_29_out, and_30_out, and_31_out, and_32_out);

  // Other names for the same wires on the sheet: Ao = A; Bo = B; Co = C; Do = D
endmodule
