// Digital circuit register-file.dig as structural Verilog
module register_file (
  input  [4:0] ReadReg1,
  input  [4:0] ReadReg2,
  input  [4:0] WriteReg,
  input  [31:0] WriteData,
  input  RegWrite,
  input  Clock,
  output [31:0] ReadData1,
  output [31:0] ReadData2
);

  wire RegWrite0, RegWrite1, RegWrite2, RegWrite3, RegWrite4, RegWrite5, RegWrite6, RegWrite7, RegWrite8,
       RegWrite9, RegWrite10, RegWrite11, RegWrite12, RegWrite13, RegWrite14, RegWrite15, RegWrite16,
       RegWrite17, RegWrite18, RegWrite19, RegWrite20, RegWrite21, RegWrite22, RegWrite23, RegWrite24,
       RegWrite25, RegWrite26, RegWrite27, RegWrite28, RegWrite29, RegWrite30, RegWrite31;
  wire [4:0] WriteTo;
  wire [31:0] r1, r2, r3, r4, r5, r6, r7, r8, r9, r10, r11, r12, r13, r14, r15, r16, r17, r18, r19, r20, r21,
       r22, r23, r24, r25, r26, r27, r28, r29, r30, r31, ro0, ro1, ro2, ro3, ro4, ro5, ro6, ro7, ro8, ro9,
       ro10, ro11, ro12, ro13, ro14, ro15, ro16, ro17, ro18, ro19, ro20, ro21, ro22, ro23, ro24, ro25, ro26,
       ro27, ro28, ro29, ro30, ro31;

  Register #(.Bits(32)) Register_0 (.D({32{1'b0}}), .C(Clock), .en(RegWrite0), .Q(ro0));
  Register #(.Bits(32)) Register_4 (.D(r4), .C(Clock), .en(RegWrite4), .Q(ro4));
  Register #(.Bits(32)) Register_8 (.D(r8), .C(Clock), .en(RegWrite8), .Q(ro8));
  Register #(.Bits(32)) Register_12 (.D(r12), .C(Clock), .en(RegWrite12), .Q(ro12));
  Register #(.Bits(32)) Register_16 (.D(r16), .C(Clock), .en(RegWrite16), .Q(ro16));
  Register #(.Bits(32)) Register_20 (.D(r20), .C(Clock), .en(RegWrite20), .Q(ro20));
  Register #(.Bits(32)) Register_24 (.D(r24), .C(Clock), .en(RegWrite24), .Q(ro24));
  Register #(.Bits(32)) Register_28 (.D(r28), .C(Clock), .en(RegWrite28), .Q(ro28));
  Register #(.Bits(32)) Register_1 (.D(r1), .C(Clock), .en(RegWrite1), .Q(ro1));
  Register #(.Bits(32)) Register_5 (.D(r5), .C(Clock), .en(RegWrite5), .Q(ro5));
  Register #(.Bits(32)) Register_9 (.D(r9), .C(Clock), .en(RegWrite9), .Q(ro9));
  Register #(.Bits(32)) Register_13 (.D(r13), .C(Clock), .en(RegWrite13), .Q(ro13));
  Register #(.Bits(32)) Register_17 (.D(r17), .C(Clock), .en(RegWrite17), .Q(ro17));
  Register #(.Bits(32)) Register_21 (.D(r21), .C(Clock), .en(RegWrite21), .Q(ro21));
  Register #(.Bits(32)) Register_25 (.D(r25), .C(Clock), .en(RegWrite25), .Q(ro25));
  Register #(.Bits(32)) Register_29 (.D(r29), .C(Clock), .en(RegWrite29), .Q(ro29));
  Multiplexer #(.Bits(5)) multiplexer_1 (.sel(RegWrite), .in_0({5{1'b0}}), .in_1(WriteReg), .out(WriteTo));
  Register #(.Bits(32)) Register_2 (.D(r2), .C(Clock), .en(RegWrite2), .Q(ro2));
  Register #(.Bits(32)) Register_6 (.D(r6), .C(Clock), .en(RegWrite6), .Q(ro6));
  Register #(.Bits(32)) Register_10 (.D(r10), .C(Clock), .en(RegWrite10), .Q(ro10));
  Register #(.Bits(32)) Register_14 (.D(r14), .C(Clock), .en(RegWrite14), .Q(ro14));
  Register #(.Bits(32)) Register_18 (.D(r18), .C(Clock), .en(RegWrite18), .Q(ro18));
  Register #(.Bits(32)) Register_22 (.D(r22), .C(Clock), .en(RegWrite22), .Q(ro22));
  Register #(.Bits(32)) Register_26 (.D(r26), .C(Clock), .en(RegWrite26), .Q(ro26));
  Register #(.Bits(32)) Register_30 (.D(r30), .C(Clock), .en(RegWrite30), .Q(ro30));
  Register #(.Bits(32)) Register_3 (.D(r3), .C(Clock), .en(RegWrite3), .Q(ro3));
  Register #(.Bits(32)) Register_7 (.D(r7), .C(Clock), .en(RegWrite7), .Q(ro7));
  Register #(.Bits(32)) Register_11 (.D(r11), .C(Clock), .en(RegWrite11), .Q(ro11));
  Register #(.Bits(32)) Register_15 (.D(r15), .C(Clock), .en(RegWrite15), .Q(ro15));
  Register #(.Bits(32)) Register_19 (.D(r19), .C(Clock), .en(RegWrite19), .Q(ro19));
  Register #(.Bits(32)) Register_23 (.D(r23), .C(Clock), .en(RegWrite23), .Q(ro23));
  Register #(.Bits(32)) Register_27 (.D(r27), .C(Clock), .en(RegWrite27), .Q(ro27));
  Register #(.Bits(32)) Register_31 (.D(r31), .C(Clock), .en(RegWrite31), .Q(ro31));
  Demultiplexer #(.Selector_Bits(5), .Bits(32)) demultiplexer_1 (
    .sel(WriteReg), .in(WriteData), .out_1(r1), .out_2(r2), .out_3(r3), .out_4(r4), .out_5(r5), .out_6(r6),
    .out_7(r7), .out_8(r8), .out_9(r9), .out_10(r10), .out_11(r11), .out_12(r12), .out_13(r13), .out_14(r14),
    .out_15(r15), .out_16(r16), .out_17(r17), .out_18(r18), .out_19(r19), .out_20(r20), .out_21(r21),
    .out_22(r22), .out_23(r23), .out_24(r24), .out_25(r25), .out_26(r26), .out_27(r27), .out_28(r28),
    .out_29(r29), .out_30(r30), .out_31(r31));  // open: out_0
  Multiplexer #(.Selector_Bits(5), .Bits(32)) multiplexer_2 (
    .sel(ReadReg1), .in_0({32{1'b0}}), .in_1(ro1), .in_2(ro2), .in_3(ro3), .in_4(ro4), .in_5(ro5),
    .in_6(ro6), .in_7(ro7), .in_8(ro8), .in_9(ro9), .in_10(ro10), .in_11(ro11), .in_12(ro12), .in_13(ro13),
    .in_14(ro14), .in_15(ro15), .in_16(ro16), .in_17(ro17), .in_18(ro18), .in_19(ro19), .in_20(ro20),
    .in_21(ro21), .in_22(ro22), .in_23(ro23), .in_24(ro24), .in_25(ro25), .in_26(ro26), .in_27(ro27),
    .in_28(ro28), .in_29(ro29), .in_30(ro30), .in_31(ro31), .out(ReadData1));
  Decoder #(.Selector_Bits(5)) decoder_1 (
    .sel(WriteTo), .out_0(RegWrite0), .out_1(RegWrite1), .out_2(RegWrite2), .out_3(RegWrite3),
    .out_4(RegWrite4), .out_5(RegWrite5), .out_6(RegWrite6), .out_7(RegWrite7), .out_8(RegWrite8),
    .out_9(RegWrite9), .out_10(RegWrite10), .out_11(RegWrite11), .out_12(RegWrite12), .out_13(RegWrite13),
    .out_14(RegWrite14), .out_15(RegWrite15), .out_16(RegWrite16), .out_17(RegWrite17), .out_18(RegWrite18),
    .out_19(RegWrite19), .out_20(RegWrite20), .out_21(RegWrite21), .out_22(RegWrite22), .out_23(RegWrite23),
    .out_24(RegWrite24), .out_25(RegWrite25), .out_26(RegWrite26), .out_27(RegWrite27), .out_28(RegWrite28),
    .out_29(RegWrite29), .out_30(RegWrite30), .out_31(RegWrite31));
  Multiplexer #(.Selector_Bits(5), .Bits(32)) multiplexer_3 (
    .sel(ReadReg2), .in_0({32{1'b0}}), .in_1(ro1), .in_2(ro2), .in_3(ro3), .in_4(ro4), .in_5(ro5),
    .in_6(ro6), .in_7(ro7), .in_8(ro8), .in_9(ro9), .in_10(ro10), .in_11(ro11), .in_12(ro12), .in_13(ro13),
    .in_14(ro14), .in_15(ro15), .in_16(ro16), .in_17(ro17), .in_18(ro18), .in_19(ro19), .in_20(ro20),
    .in_21(ro21), .in_22(ro22), .in_23(ro23), .in_24(ro24), .in_25(ro25), .in_26(ro26), .in_27(ro27),
    .in_28(ro28), .in_29(ro29), .in_30(ro30), .in_31(ro31), .out(ReadData2));

  // Other names for the same wires on the sheet: clk = Clock; RData1[31:0] = ReadData1; RData2[31:0] = ReadData2;
  //   RReg1[4:0] = ReadReg1; RReg2[4:0] = ReadReg2; RWrite = RegWrite; WData[31:0] = WriteData; WReg[4:0] = WriteReg
endmodule

/* Test case Register File Test:
WriteReg WriteData RegWrite Clock ReadReg1 ReadReg2 ReadData1 ReadData2

# $1 = 25
1 25 1 C 1 0 25 0

# $2 = 30
2 30 1 C 0 2 0 30

# $(N+1) = (N+1)
loop(N, 30)
	(N+1) (N+1) 1 C (N+1) (N) (N+1) (N)
end loop

# $(N+1) = N-60
loop(N, 30)
	(N+1) (N-60) 1 C (N+1) (N+1) (N-60) (N-60)
end loop

# Try writing to $0. This should not write anything
0 25 1 C 0 0 0 0

# try writing when RegWrite = 0
# (the registers should still have their old values)
loop(N, 30)
	(N+1) (N+80) 0 C (N+1) (N+1) (N-60) (N-60)
end loop
*/
